// Logisim project Lab3z1.circ as structural Verilog: 1 circuit, main circuit main
module main (
);

  wire A_out, B_out, C_out, D_out, dipswitch_1_p1, dipswitch_1_p2, dipswitch_1_p3, E_out, F_out, G_out,
       H_out, I_out;

  // DipSwitch #(.number(3)) dipswitch_1: pin names not known; wires that end beside it: dipswitch_1_p1, dipswitch_1_p2, dipswitch_1_p3
  nand A (A_out, dipswitch_1_p1, dipswitch_1_p2);
  nand B (B_out, dipswitch_1_p1, A_out);
  nand C (C_out, A_out, dipswitch_1_p2);
  nand D (D_out, B_out, C_out);
  nand E (E_out, D_out, dipswitch_1_p3);
  nand F (F_out, D_out, E_out);
  nand G (G_out, E_out, dipswitch_1_p3);
  nand H (H_out, E_out, A_out);
  LED led_1 (.in(H_out));
  nand I (I_out, F_out, G_out);
  LED led_2 (.in(I_out));

  // Notes on the sheet:
  //   A
  //   B
  //   C_in
  //   Pom
  //   Pom
  //   Pom
  //   C_out
  //   Sum
endmodule
