// Logisim project Lab3z2.circ as structural Verilog: 1 circuit, main circuit main
module main (
);

  wire dipswitch_1_p1, dipswitch_1_p2, dipswitch_1_p3, nand_1_out, nand_2_out, nand_3_out, nor_1_out,
       not_1_out, not_2_out, slider_1_out;

  // DipSwitch #(.number(3)) dipswitch_1: pin names not known; wires that end beside it: dipswitch_1_p1, dipswitch_1_p2, dipswitch_1_p3
  nor nor_1 (nor_1_out, dipswitch_1_p1, dipswitch_1_p2, dipswitch_1_p3);
  Slider #(.width(1)) slider_1 (.out(slider_1_out));
  not not_1 (not_1_out, nor_1_out);
  nand nand_1 (nand_1_out, slider_1_out, not_1_out);
  not not_2 (not_2_out, slider_1_out);
  nand nand_2 (nand_2_out, not_2_out, nor_1_out);
  nand nand_3 (nand_3_out, nand_1_out, nand_2_out);
  LED led_1 (.in(nand_3_out));

  // Notes on the sheet:
  //   S
  //   A
  //   B
  //   C
  //   Y = A*!S +B*S
  //   Y = !(!(A*S)*!(B*!S)
  //   Y
endmodule
